# Fritzing sketch MatulaCircuit (saved by Fritzing 0.9.3b)
breadboards: 1

parts:
  DRV_1 = DRV 8825 Stepper Motor Carrier, High Current [part_number="DRV 8825"]
  DRV_2 = DRV 8825 Stepper Motor Carrier, High Current [part_number="DRV 8825"]
  DRV_3 = DRV 8825 Stepper Motor Carrier, High Current [part_number="DRV 8825"]
  IC1 = L293D [package=THT]
  C1 = Capacitor Polarized [package=nippon_f80]
  C2 = Capacitor Polarized [package=nippon_f80]
  C3 = Capacitor Polarized [package=nippon_f80]
  Componente2 = Arduino Mega 2560 (Rev3)
  J1 = Power Jack [package=power_jack_pth_lock]  # not connected
  M1 = DC Motor
  M2 = Stepper Motor - Bipolar
  M3 = Stepper Motor - Bipolar
  M4 = Stepper Motor - Bipolar
  C5 = Capacitor Polarized [package=nippon_f80]
  Componente4 = Arduino Board Ethernet

nets:
  N1: DRV_1.ENABLE, Componente2.D38
  3.3V: DRV_1.RESET, DRV_1.SLEEP, DRV_2.RESET, DRV_2.SLEEP, DRV_3.RESET, DRV_3.SLEEP, IC1.Enable_1
  N2: DRV_1.STEP, Componente2.D39
  N3: DRV_1.DIRECTION, Componente2.D40
  9V: DRV_1.VOLTAGE_ST/_MT, DRV_2.VOLTAGE_ST/_MT, DRV_3.VOLTAGE_ST/_MT, IC1.+Vmotor, C1.+, C2.+, C3.+, C5.+
  GND: DRV_1.GROUND_ST/_MT, DRV_1.GROUND_LOG, DRV_2.GROUND_ST/_MT, DRV_2.GROUND_LOG, DRV_3.GROUND_ST/_MT, DRV_3.GROUND_LOG, IC1.0V, C1.-, C2.-, C3.-, Componente2.GND, C5.-
  N4: DRV_1.OUT_2B, M2.A
  N5: DRV_1.OUT_2A, M2.C
  N6: DRV_1.OUT_1A, M2.B
  N7: DRV_1.OUT_1B, M2.D
  N8: DRV_2.ENABLE, Componente2.D47
  N9: DRV_2.STEP, Componente2.D49
  N10: DRV_2.DIRECTION, Componente2.D50
  N11: DRV_2.OUT_2B, M3.A
  N12: DRV_2.OUT_2A, M3.C
  N13: DRV_2.OUT_1A, M3.B
  N14: DRV_2.OUT_1B, M3.D
  N15: DRV_3.ENABLE, Componente2.D42
  N16: DRV_3.STEP, Componente2.D44
  N17: DRV_3.DIRECTION, Componente2.D45
  N18: DRV_3.OUT_2B, M4.A
  N19: DRV_3.OUT_2A, M4.C
  N20: DRV_3.OUT_1A, M4.B
  N21: DRV_3.OUT_1B, M4.D
  N22: IC1.In_1, Componente2.D53
  N23: IC1.Out_1_(_Controlled_by_Enable_1_), M1.pin_1
  N24: IC1.Out_2_(_Controlled_by_Enable_1_), M1.pin_2
  N25: IC1.In_2, Componente2.D52
  N26: Componente2.D13_PWM, Componente4.D13/SCK
  N27: Componente2.D12_PWM, Componente4.D12/MISO
  N28: Componente2.D11_PWM, Componente4.D11/MOSI
  N29: Componente2.D10_PWM, Componente4.D10_PWM/SS
  5V: Componente2.VIN, Componente4.VIN
